# Fritzing sketch FM Radio (saved by Fritzing 0.9.3b)
breadboards: 1

parts:
  Parça1 = Arduino Uno (Rev3)
  LCD1 = LCD screen
  R1_(Ekran) = Rotary Potentiometer (Small) [maximum_resistance=100kΩ package=THT]
  R2_(Kanal_switch) = Rotary Potentiometer (Small) [maximum_resistance=100kΩ package=THT]
  IC1 = DIP - 10 pins [chip_label=TEA5767 package="DIP (Dual Inline) [THT]"]

nets:
  N1: Parça1.A0, R2_(Kanal_switch).wiper
  N2: Parça1.A4/SDA, IC1.DATA
  N3: Parça1.A5/SCL, IC1.SCLK
  N4: Parça1.D11_PWM/MOSI, LCD1.E
  N5: Parça1.D12/MISO, LCD1.RS
  N6: Parça1.D2, LCD1.DB7
  N7: Parça1.D3_PWM, LCD1.DB6
  N8: Parça1.D4, LCD1.DB5
  N9: Parça1.D5_PWM, LCD1.DB4
  5V: Parça1.5V, LCD1.VDD, LCD1.LED+, R1_(Ekran).leg1, R2_(Kanal_switch).leg1, IC1.VCC
  GND: Parça1.GND, LCD1.VSS, LCD1.R/W, LCD1.LED-, R1_(Ekran).leg2, R2_(Kanal_switch).leg2, IC1.GND
  N10: LCD1.V0, R1_(Ekran).wiper

custom parts:
  DIP - 10 pins: A DIP stand-in part for whatever IC you want. With 10 pins on a 300mil dual inline package (DIP) footprint.

// code stored in the sketch: kod.ino
#include <Wire.h>
#include <LiquidCrystal.h>

unsigned char frekansH = 0;
unsigned char frekansL = 0;

unsigned int frekansB;
double frekans = 0;

static char frekans_ekran[15];

LiquidCrystal lcd(12, 11, 5, 4, 3, 2);

void setup()
{
  Wire.begin();
  lcd.begin(16, 2);
  frekans = 93.0;
  frekansAyarla();
  lcd.setCursor(3, 0);
  lcd.print("FM Radyo");
}

void loop()
{
  int reading = analogRead(0);
  frekans = ((double)reading * (108.0 - 87.5)) / 1024.0 + 87.5;
  frekans = ((int)(frekans * 10)) / 10.0;
  frekansAyarla();
  dtostrf(frekans, 6, 2, frekans_ekran);
  lcd.setCursor(4, 1);
  lcd.print(frekans_ekran);
}

void frekansAyarla()
{
  frekansB = 4 * (frekans * 1000000 + 225000) / 32768;
  frekansH = frekansB >> 8;
  frekansL = frekansB & 0XFF;
  delay(100);
  Wire.beginTransmission(0x60);
  Wire.write(frekansH);
  Wire.write(frekansL);
  Wire.write(0xB0);
  Wire.write(0x10);
  Wire.write((byte)0x00);
  Wire.endTransmission();
  delay(100);
}
